// Logisim project intcode.circ as structural Verilog: 7 circuits, main circuit alu
module main_computer (
);

  wire clear_out, clock_1_out, clr_keys_out, cpu_1_key_enable, cpu_1_new_output, cpu_1_read_write,
       keyboard_1_avail, not_1_out;
  wire [3:0] display_formatter_1_high_nibble, display_formatter_1_low_nibble, display_formatter_1_out_4,
       display_formatter_1_out_5, display_formatter_1_out_6, display_formatter_1_out_7,
       display_formatter_1_out_8, display_formatter_1_out_9;
  wire [6:0] display_formatter_1_ascii_out, keyboard_1_data;
  wire [15:0] cpu_1_address;
  wire [31:0] controlled_buffer_1_out, controlled_buffer_2_out, cpu_1_data_out, cpu_1_output;

  assign controlled_buffer_1_out = not_1_out ? cpu_1_data_out : 32'bz;  // Controlled_Buffer controlled_buffer_1
  assign controlled_buffer_2_out = cpu_1_read_write ? controlled_buffer_1_out : 32'bz;  // Controlled_Buffer controlled_buffer_2
  not not_1 (not_1_out, cpu_1_read_write);
  Button clear (.out(clear_out));
  Clock clock_1 (.out(clock_1_out));
  Button clr_keys (.out(clr_keys_out));
  Keyboard keyboard_1 (
    .clk(clock_1_out), .re(cpu_1_key_enable), .clr(clr_keys_out), .avail(keyboard_1_avail),
    .data(keyboard_1_data));
  cpu cpu_1 (
    .key_input(keyboard_1_data), .clk(clock_1_out), .buffer_contains(keyboard_1_avail),
    .data_in(controlled_buffer_2_out), .key_enable(cpu_1_key_enable), .address(cpu_1_address),
    .read_write(cpu_1_read_write), .\output (cpu_1_output), .clr(clear_out), .new_output(cpu_1_new_output),
    .data_out(cpu_1_data_out), .num_char(1'b0));
  RAM #(.addrWidth(16), .dataWidth(32)) ram_1 (
    .addr(cpu_1_address), .data(controlled_buffer_1_out), .clk(clock_1_out), .ld(cpu_1_read_write));  // open: sel, clr
  display_formatter display_formatter_1 (
    .data(cpu_1_output), .ascii_out(display_formatter_1_ascii_out),
    .high_nibble(display_formatter_1_high_nibble), .out_4(display_formatter_1_out_4),
    .out_5(display_formatter_1_out_5), .out_6(display_formatter_1_out_6), .out_7(display_formatter_1_out_7),
    .out_8(display_formatter_1_out_8), .out_9(display_formatter_1_out_9),
    .low_nibble(display_formatter_1_low_nibble));
  // Probe on display_formatter_1_ascii_out
  TTY #(.rows(20), .cols(75)) tty_1 (
    .data(display_formatter_1_ascii_out), .clk(clock_1_out), .we(cpu_1_new_output));  // open: clr
  Hex_Digit_Display hex_digit_display_1 (.value(display_formatter_1_high_nibble));  // open: dp
  Hex_Digit_Display hex_digit_display_2 (.value(display_formatter_1_out_5));  // open: dp
  Hex_Digit_Display hex_digit_display_3 (.value(display_formatter_1_out_4));  // open: dp
  Hex_Digit_Display hex_digit_display_4 (.value(display_formatter_1_out_6));  // open: dp
  Hex_Digit_Display hex_digit_display_5 (.value(display_formatter_1_out_7));  // open: dp
  Hex_Digit_Display hex_digit_display_6 (.value(display_formatter_1_out_9));  // open: dp
  Hex_Digit_Display hex_digit_display_7 (.value(display_formatter_1_out_8));  // open: dp
  Hex_Digit_Display hex_digit_display_8 (.value(display_formatter_1_low_nibble));  // open: dp

  // Notes on the sheet:
  //   INTCODE COMPUTER 32-bit
  //   Set this to one to read input
  //   as number and zero to read as char
  //   instruction RAM
  //   Terminal Output/Hex Codes
endmodule

module cpu (
  input  [6:0] key_input,
  input  buffer_contains,
  input  clk,
  input  num_char,
  input  [31:0] data_in,
  input  clr,
  output key_enable,
  output [15:0] address,
  output read_write,
  output [31:0] data_out,
  output [31:0] \output ,
  output new_output
);

  wire alu, and_1_out, and_3_out, and_4_out, and_5_out, comparator_1_eq, comparator_2_eq, comparator_3_eq,
       comparator_4_eq, comparator_5_eq, comparator_6_eq, comparator_7_eq, comparator_8_eq, comparator_9_eq,
       comparator_10_eq, comparator_11_eq, comparator_12_eq, comparator_13_eq, comparator_14_eq,
       comparator_15_eq, data, incPC, loadBase, loadIR, loadPC, loadR1, loadR2, loadR3, loadTR, not_1_out,
       not_2_out, not_3_out, or_3_out, or_5_out, or_6_out, t0, t1, t2, t3, t4, t5, t6, t7;
  wire [7:0] op, sc;
  wire [31:0] adder_1_out, adder_2_out, adder_3_out, adder_4_out, alu_1_out_6, arg_parser_1_output1,
       arg_parser_1_output2, arg_parser_1_output3, base, inp, input_circuit_1_inp, ir, multiplexer_1_out,
       multiplexer_3_out, pc, pc_increment_1_addend, r1, r2, r3;
  wire [31:8] divider_1_rem;
  wire [31:16] multiplexer_2_out;

  // Probe on clk
  Comparator comparator_1 (.a(op), .b(8'h9), .eq(comparator_1_eq));  // open: gt, lt
  Comparator comparator_2 (.a(op), .b(8'h3), .eq(comparator_2_eq));  // open: gt, lt
  Divider #(.width(32)) divider_1 (.a(ir), .b(32'h64), .rem({divider_1_rem, op}));  // open: out, upper
  Multiplexer #(.width(32)) multiplexer_1 (
    .in0(r2), .in1(base), .out(multiplexer_1_out), .sel(comparator_1_eq));  // open: en
  buf buffer_1 (loadIR, t0);
  buf buffer_2 (loadR3, t3);
  and and_1 (and_1_out, t4, not_1_out);
  not not_1 (not_1_out, comparator_2_eq);
  // Probe on alu_1_out_6
  alu alu_1 (.opcode(ir), .arg1(r1), .arg2(multiplexer_1_out), .out_6(alu_1_out_6), .input_reg(inp), .pc(pc));
  or or_1 (loadR2, t5, t2);
  or or_2 (loadR1, t1, and_1_out);
  assign data_out = data ? data_in : 32'bz;  // Controlled_Buffer controlled_buffer_1
  assign data_out = alu ? alu_1_out_6 : 32'bz;  // Controlled_Buffer controlled_buffer_2
  pc_increment pc_increment_1 (.opc(ir), .addend(pc_increment_1_addend));  // open: halt
  assign data_out = incPC ? adder_1_out : 32'bz;  // Controlled_Buffer controlled_buffer_3
  Register #(.width(32)) register_1 (.D(data_out), .en(loadPC), .Q(pc), .clk(clk), .clr(clr));
  Register #(.width(32)) register_2 (.D(data_out), .en(loadR1), .Q(r1), .clk(clk), .clr(clr));
  Register #(.width(32)) register_3 (.D(data_out), .en(loadR2), .Q(r2), .clk(clk));  // open: clr
  Register #(.width(32)) register_4 (.D(data_out), .en(loadR3), .Q(r3), .clk(clk), .clr(clr));
  Register #(.width(32)) register_5 (.D(data_out), .en(loadIR), .Q(ir), .clk(clk), .clr(clr));
  Register #(.width(32)) register_6 (.D(data_out), .en(loadBase), .Q(base), .clk(clk), .clr(clr));
  Register #(.width(32)) register_7 (.D(data_out), .en(loadTR), .Q(\output ), .clk(clk));  // open: clr
  input_circuit input_circuit_1 (.keyport(key_input), .number_char(num_char), .inp(input_circuit_1_inp));
  Adder #(.width(32)) adder_1 (.a(pc_increment_1_addend), .b(pc), .out(adder_1_out));  // open: cin, cout
  Counter #(.width(32), .max('hffffffff)) input_r (
    .load(1'b1), .D(input_circuit_1_inp), .count(1'b0), .Q(inp), .clk(clk), .clr(clr));  // open: carry
  Adder #(.width(32)) adder_2 (.a(pc), .b(32'h1), .out(adder_2_out));  // open: cin, cout
  Adder #(.width(32)) adder_3 (.a(pc), .b(32'h2), .out(adder_3_out));  // open: cin, cout
  Adder #(.width(32)) adder_4 (.a(pc), .b(32'h3), .out(adder_4_out));  // open: cin, cout
  arg_parser arg_parser_1 (
    .base(base), .pc(pc), .output1(arg_parser_1_output1), .output2(arg_parser_1_output2),
    .output3(arg_parser_1_output3), .arg1(r1), .arg2(r2), .arg3(r3), .opcode(ir));
  Comparator comparator_3 (.a(op), .b(8'h3), .eq(comparator_3_eq));  // open: gt, lt
  Comparator comparator_4 (.a(op), .b(8'h3), .eq(comparator_4_eq));  // open: gt, lt
  Multiplexer #(.select(4), .width(32)) multiplexer_2 (
    .in0(pc), .in1(adder_2_out), .in2(adder_3_out), .in3(adder_4_out), .in4(arg_parser_1_output1),
    .in5(arg_parser_1_output2), .in6(multiplexer_3_out), .out({multiplexer_2_out, address}), .sel(sc[3:0]));  // open: in7, in8, in9, in10, in11, in12, in13, in14, in15, en
  Multiplexer #(.width(32)) multiplexer_3 (
    .in0(arg_parser_1_output3), .in1(arg_parser_1_output1), .out(multiplexer_3_out), .sel(comparator_3_eq));  // open: en
  buf buffer_3 (alu, t6);
  Comparator comparator_5 (.a(op), .b(8'h5), .eq(comparator_5_eq));  // open: gt, lt
  Comparator comparator_6 (.a(op), .b(8'h6), .eq(comparator_6_eq));  // open: gt, lt
  and and_2 (key_enable, t5, comparator_4_eq, 1'b1);
  Comparator comparator_7 (.a(op), .b(8'h3), .eq(comparator_7_eq));  // open: gt, lt
  not not_2 (not_2_out, buffer_contains);
  and and_3 (and_3_out, t6, or_3_out);
  or or_3 (or_3_out, comparator_5_eq, comparator_6_eq);
  and and_4 (and_4_out, t4, comparator_7_eq, not_2_out);
  Comparator comparator_8 (.a(op), .b(8'h63), .eq(comparator_8_eq));  // open: gt, lt
  or or_4 (loadPC, and_3_out, t7);
  buf buffer_4 (incPC, t7);
  not not_3 (not_3_out, or_5_out);
  or or_5 (or_5_out, and_4_out, comparator_8_eq);
  Comparator comparator_9 (.a(op), .b(8'h4), .eq(comparator_9_eq));  // open: gt, lt
  Comparator comparator_10 (.a(op), .b(8'h5), .eq(comparator_10_eq));  // open: gt, lt
  Comparator comparator_11 (.a(op), .b(8'h6), .eq(comparator_11_eq));  // open: gt, lt
  Comparator comparator_12 (.a(op), .b(8'h9), .eq(comparator_12_eq));  // open: gt, lt
  Counter #(.max('h7)) counter_1 (.count(not_3_out), .Q(sc), .clk(clk), .clr(clr));  // open: load, D, carry
  or or_6 (or_6_out, comparator_9_eq, comparator_10_eq, comparator_11_eq, comparator_12_eq);
  // Probe on sc[3:0]
  Decoder #(.select(4), .enable("false")) decoder_1 (
    .out0(t0), .out1(t1), .out2(t2), .out3(t3), .out4(t4), .out5(t5), .out6(t6), .out7(t7), .sel(sc[3:0]));  // open: out8, out9, out10, out11, out12, out13, out14, out15
  or or_7 (data, t0, t1, t2, t3, t4, t5);
  and and_5 (and_5_out, t6, or_6_out);
  Comparator comparator_13 (.a(op), .b(8'h9), .eq(comparator_13_eq));  // open: gt, lt
  Comparator comparator_14 (.a(op), .b(8'h4), .eq(comparator_14_eq));  // open: gt, lt
  Comparator comparator_15 (.a(op), .b(8'h4), .eq(comparator_15_eq));  // open: gt, lt
  or or_8 (read_write, data, and_5_out);
  and and_6 (loadBase, t6, comparator_13_eq);
  and and_7 (loadTR, t6, comparator_14_eq);
  and and_8 (new_output, t7, comparator_15_eq);

  // Other names for the same wires on the sheet: addr[15:0] = address; buffer_t = buffer_contains;
  //   k_enable = key_enable; ldMem = read_write

  // Notes on the sheet:
  //   CCL and Datapath
  //   Register load control
  //   data bus
  //   instruction RAM
  //   input control
  //   address control
  //   pc control
  //   or a halt
  //   control logic for memory
  //   sequence counter control
  //   should count unless the input is empty on an input stage
  //   output and base load
endmodule

module alu (
  input  [31:0] opcode,
  input  [31:0] pc,
  input  [31:0] arg1,
  input  [31:0] arg2,
  input  [31:0] input_reg,
  output [31:0] out_6
);

  wire comparator_1_eq, comparator_2_eq, comparator_2_lt;
  wire [3:0] bitselector_1_out;
  wire [31:0] adder_1_out, adder_2_out, bit_extender_3_out, bit_extender_4_out, divider_1_rem,
       multiplexer_1_out, multiplexer_2_out, multiplier_1_out;

  Bit_Extender #(.in_width(1), .out_width(32)) bit_extender_1 ();  // open: in, out
  Bit_Extender #(.in_width(1), .out_width(32)) bit_extender_2 ();  // open: in, out
  Comparator #(.width(32)) comparator_1 (.a(arg1), .b({32{1'b0}}), .eq(comparator_1_eq));  // open: gt, lt
  Divider #(.width(32)) divider_1 (.a(opcode), .b(32'h64), .rem(divider_1_rem));  // open: out, upper
  Adder #(.width(32)) adder_1 (.a(pc), .b(32'h3), .out(adder_1_out));  // open: cin, cout
  Comparator #(.width(32)) comparator_2 (.a(arg1), .b(arg2), .eq(comparator_2_eq), .lt(comparator_2_lt));  // open: gt
  BitSelector #(.width(32), .group(4)) bitselector_1 (.in(divider_1_rem), .out(bitselector_1_out), .sel(3'b000));
  Adder #(.width(32)) adder_2 (.a(arg1), .b(arg2), .out(adder_2_out));  // open: cin, cout
  Multiplier #(.width(32)) multiplier_1 (.a(arg1), .b(arg2), .out(multiplier_1_out));  // open: cin, cout
  Multiplexer #(.width(32)) multiplexer_1 (
    .in0(arg2), .in1(adder_1_out), .out(multiplexer_1_out), .sel(comparator_1_eq));  // open: en
  Multiplexer #(.width(32)) multiplexer_2 (
    .in0(adder_1_out), .in1(arg2), .out(multiplexer_2_out), .sel(comparator_1_eq));  // open: en
  assign bit_extender_3_out = {{31{1'b0}}, comparator_2_lt};  // Bit_Extender bit_extender_3
  assign bit_extender_4_out = {{31{1'b0}}, comparator_2_eq};  // Bit_Extender bit_extender_4
  Multiplexer #(.select(4), .width(32)) multiplexer_3 (
    .in1(adder_2_out), .in2(multiplier_1_out), .in3(input_reg), .in4(arg1), .in5(multiplexer_1_out),
    .in6(multiplexer_2_out), .in7(bit_extender_3_out), .in8(bit_extender_4_out), .in9(adder_2_out),
    .out(out_6), .sel(bitselector_1_out));  // open: in0, in10, in11, in12, in13, in14, in15, en

  // Other names for the same wires on the sheet: aluA1[31:0] = arg1; aluA2[31:0] = arg2; aluInput[31:0] = input_reg;
  //   aluPC[31:0] = pc

  // Notes on the sheet:
  //   need to wire base to arg2 in the 9 case
  //   ALU provides assignment/output based on opcode
endmodule

module arg_parser (
  input  [31:0] base,
  input  [31:0] pc,
  input  [31:0] opcode,
  input  [31:0] arg1,
  input  [31:0] arg2,
  input  [31:0] arg3,
  output [31:0] output1,
  output [31:0] output2,
  output [31:0] output3
);

  wire comparator_1_eq, comparator_1_gt, comparator_1_lt, comparator_2_eq, comparator_2_gt, comparator_3_eq,
       comparator_3_gt, comparator_3_lt, comparator_4_eq, comparator_4_gt, comparator_5_eq, comparator_5_gt,
       comparator_5_lt, comparator_6_eq, comparator_6_gt, or_1_out, or_2_out, or_3_out, or_4_out, or_5_out,
       or_6_out;
  wire [1:0] priority_encoder_1_out, priority_encoder_2_out, priority_encoder_3_out;
  wire [31:0] adder_1_out, adder_2_out, adder_3_out, adder_4_out, adder_5_out, adder_6_out, divider_1_rem,
       divider_2_rem, divider_3_rem;

  Divider #(.width(32)) divider_1 (.a(opcode), .b(32'h3e8), .rem(divider_1_rem));  // open: out, upper
  Divider #(.width(32)) divider_2 (.a(opcode), .b(32'h2710), .rem(divider_2_rem));  // open: out, upper
  Divider #(.width(32)) divider_3 (.a(opcode), .b(32'h186a0), .rem(divider_3_rem));  // open: out, upper
  Comparator #(.width(32)) comparator_1 (
    .a(divider_1_rem), .b(32'h64), .gt(comparator_1_gt), .eq(comparator_1_eq), .lt(comparator_1_lt));
  Comparator #(.width(32)) comparator_2 (
    .a(divider_1_rem), .b(32'hc8), .gt(comparator_2_gt), .eq(comparator_2_eq));  // open: lt
  Comparator #(.width(32)) comparator_3 (
    .a(divider_2_rem), .b(32'h3e8), .gt(comparator_3_gt), .eq(comparator_3_eq), .lt(comparator_3_lt));
  Comparator #(.width(32)) comparator_4 (
    .a(divider_2_rem), .b(32'h7d0), .gt(comparator_4_gt), .eq(comparator_4_eq));  // open: lt
  Comparator #(.width(32)) comparator_5 (
    .a(divider_3_rem), .b(32'h2710), .gt(comparator_5_gt), .eq(comparator_5_eq), .lt(comparator_5_lt));
  Comparator #(.width(32)) comparator_6 (
    .a(divider_3_rem), .b(32'h4e20), .gt(comparator_6_gt), .eq(comparator_6_eq));  // open: lt
  or or_1 (or_1_out, comparator_2_gt, comparator_2_eq);
  or or_2 (or_2_out, comparator_3_gt, comparator_3_eq);
  or or_3 (or_3_out, comparator_4_gt, comparator_4_eq);
  or or_4 (or_4_out, comparator_5_gt, comparator_5_eq);
  or or_5 (or_5_out, comparator_6_gt, comparator_6_eq);
  Adder #(.width(32)) adder_1 (.a(pc), .b(32'h1), .out(adder_1_out));  // open: cin, cout
  or or_6 (or_6_out, comparator_1_gt, comparator_1_eq);
  Priority_Encoder #(.select(2)) priority_encoder_1 (
    .in0(comparator_1_lt), .in1(or_6_out), .in2(or_1_out), .out(priority_encoder_1_out));  // open: in3, gs, en_out, en_in
  Adder #(.width(32)) adder_2 (.a(base), .b(arg1), .out(adder_2_out));  // open: cin, cout
  Priority_Encoder #(.select(2)) priority_encoder_2 (
    .in0(comparator_3_lt), .in1(or_2_out), .in2(or_3_out), .out(priority_encoder_2_out));  // open: in3, gs, en_out, en_in
  Adder #(.width(32)) adder_3 (.a(adder_1_out), .b(32'h1), .out(adder_3_out));  // open: cin, cout
  Adder #(.width(32)) adder_4 (.a(base), .b(arg2), .out(adder_4_out));  // open: cin, cout
  Multiplexer #(.select(2), .width(32), .enable("false")) multiplexer_1 (
    .in0(arg1), .in1(adder_1_out), .in2(adder_2_out), .out(output1), .sel(priority_encoder_1_out));  // open: in3
  Adder #(.width(32)) adder_5 (.a(adder_3_out), .b(32'h1), .out(adder_5_out));  // open: cin, cout
  Adder #(.width(32)) adder_6 (.a(base), .b(arg3), .out(adder_6_out));  // open: cin, cout
  Multiplexer #(.select(2), .width(32), .enable("false")) multiplexer_2 (
    .in0(arg2), .in1(adder_3_out), .in2(adder_4_out), .out(output2), .sel(priority_encoder_2_out));  // open: in3
  Priority_Encoder #(.select(2)) priority_encoder_3 (
    .in0(comparator_5_lt), .in1(or_4_out), .in2(or_5_out), .out(priority_encoder_3_out));  // open: in3, gs, en_out, en_in
  Multiplexer #(.select(2), .width(32), .enable("false")) multiplexer_3 (
    .in0(arg3), .in1(adder_5_out), .in2(adder_6_out), .out(output3), .sel(priority_encoder_3_out));  // open: in3

  // Notes on the sheet:
  //   Argument parser outputs the addresses that should be accessed
endmodule

module display_formatter (
  input  [31:0] data,
  output [6:0] ascii_out,
  output [3:0] high_nibble,
  output [3:0] out_4,
  output [3:0] out_5,
  output [3:0] out_6,
  output [3:0] out_7,
  output [3:0] out_8,
  output [3:0] out_9,
  output [3:0] low_nibble
);

  BitSelector #(.width(32), .group(7)) bitselector_1 (.in(data), .out(ascii_out), .sel(3'b000));

  assign high_nibble = data[31:28];
  assign low_nibble = data[3:0];
  assign out_4 = data[27:24];
  assign out_5 = data[23:20];
  assign out_6 = data[19:16];
  assign out_7 = data[15:12];
  assign out_8 = data[11:8];
  assign out_9 = data[7:4];

  // Notes on the sheet:
  //   splits off into ASCII and hex codes
endmodule

module input_circuit (
  input  [6:0] keyport,
  input  number_char,
  output [31:0] inp
);

  wire [31:0] bit_extender_1_out, multiplexer_1_out;

  assign bit_extender_1_out = {{25{1'b0}}, keyport};  // Bit_Extender bit_extender_1
  Multiplexer #(.width(32)) multiplexer_1 (
    .in0({32{1'b0}}), .in1(32'h30), .out(multiplexer_1_out), .sel(number_char));  // open: en
  Subtractor #(.width(32)) subtractor_1 (.a(bit_extender_1_out), .b(multiplexer_1_out), .out(inp));  // open: bin, bout

  // Notes on the sheet:
  //   converts keyboard input to expanded ascii or number based on pin
endmodule

module pc_increment (
  input  [31:0] opc,
  output [31:0] addend,
  output halt
);

  wire comparator_1_eq, comparator_2_eq, comparator_3_eq, comparator_4_eq, comparator_5_eq, comparator_6_eq,
       comparator_7_eq, comparator_8_eq, comparator_9_eq, or_1_out, or_2_out, or_3_out;
  wire [2:0] priority_encoder_1_out;
  wire [31:0] divider_1_rem;

  Divider #(.width(32)) divider_1 (.a(opc), .b(32'h64), .rem(divider_1_rem));  // open: out, upper
  Comparator #(.width(32)) comparator_1 (.a(divider_1_rem), .b(32'h1), .eq(comparator_1_eq));  // open: gt, lt
  Comparator #(.width(32)) comparator_2 (.a(divider_1_rem), .b(32'h2), .eq(comparator_2_eq));  // open: gt, lt
  Comparator #(.width(32)) comparator_3 (.a(divider_1_rem), .b(32'h3), .eq(comparator_3_eq));  // open: gt, lt
  Comparator #(.width(32)) comparator_4 (.a(divider_1_rem), .b(32'h4), .eq(comparator_4_eq));  // open: gt, lt
  Comparator #(.width(32)) comparator_5 (.a(divider_1_rem), .b(32'h5), .eq(comparator_5_eq));  // open: gt, lt
  Comparator #(.width(32)) comparator_6 (.a(divider_1_rem), .b(32'h6), .eq(comparator_6_eq));  // open: gt, lt
  Comparator #(.width(32)) comparator_7 (.a(divider_1_rem), .b(32'h7), .eq(comparator_7_eq));  // open: gt, lt
  Comparator #(.width(32)) comparator_8 (.a(divider_1_rem), .b(32'h8), .eq(comparator_8_eq));  // open: gt, lt
  Comparator #(.width(32)) comparator_9 (.a(divider_1_rem), .b(32'h9), .eq(comparator_9_eq));  // open: gt, lt
  Comparator #(.width(32)) comparator_10 (.a(divider_1_rem), .b(32'h63), .eq(halt));  // open: gt, lt
  or or_1 (or_1_out, comparator_1_eq, comparator_2_eq, comparator_7_eq, comparator_8_eq);
  or or_2 (or_2_out, comparator_3_eq, comparator_4_eq, comparator_9_eq);
  or or_3 (or_3_out, comparator_5_eq, comparator_6_eq);
  Priority_Encoder priority_encoder_1 (
    .in0(or_3_out), .in1(1'b0), .in2(or_2_out), .in3(1'b0), .in4(or_1_out), .in5(1'b0), .in6(1'b0),
    .in7(1'b0), .out(priority_encoder_1_out));  // open: en_in, gs, en_out
  assign addend = {{29{1'b0}}, priority_encoder_1_out};  // Bit_Extender bit_extender_1

  // Notes on the sheet:
  //   opcode
  //   provides amount pc should increase by, assuming successful op, not concerned with jump command
endmodule
